# Fritzing sketch GAMELIN_USB (saved by Fritzing 0.9.3b)
circuit board: 7.85748cm x 10.287cm
breadboards: 1

parts:
  OUT = Audio Jack (TRS) 3.5mm [package="4Ucon 08780 [THT]"]
  S1 = SWITCH-DPDT [package=eg2211]
  USB-B = USB connector [package=THT]
  3V6 = Zener Diode [part_number=1N4732A breakdown_voltage=3.6V package="300 mil [THT]"]
  3V6_2 = Zener Diode [part_number=1N4732A breakdown_voltage=3.6V package="300 mil [THT]"]
  7/12V = Power plug
  J1 = male pin header, 9 pins [form="♂ (male)"]
  Pad1 = Pad [width=1.6000000000000001 height=3.2999999999999998 connect=center]
  Pad2 = Pad [width=1.6000000000000001 height=3.2999999999999998 connect=center]
  Pad3 = Pad [width=1.6000000000000001 height=3.2999999999999998 connect=center]
  Pad4 = Pad [width=1.6000000000000001 height=3.2999999999999998 connect=center]
  Pad5 = Pad [width=1.6000000000000001 height=3.2999999999999998 connect=center]
  Pad6 = Pad [width=1.6000000000000001 height=3.2999999999999998 connect=center]
  BAT2 = BC9VPC [package=bc9vpc]
  1K5Ω = Resistor [tolerance=±5% resistance=1.5k package=THT]
  1K5Ω_2 = Resistor [tolerance=±5% resistance=1.5k package=THT]
  68Ω = Resistor [tolerance=±5% resistance=68 package=THT]
  68Ω_2 = Resistor [tolerance=±5% resistance=68 package=THT]
  330Ω = Resistor [tolerance=±5% resistance=330 package=THT]
  1N4007 = Rectifier Diode [part_number=1N4001 package="300 mil [THT]"]
  ring = female pin header, 1 pin [form="♀ (female)"]
  LED1 = smd LED [color="Red (633nm)" package="1206 [SMD]"]
  BC548 = NPN-Transistor [package="TO92 [THT]"]
  1KΩ = Resistor [tolerance=±5% resistance=1k package=THT]
  Pad7 = Pad [width=2.4466785185185205 height=2.5474130370370385 connect=center]
  Pad8 = Pad [width=2.4466785185185205 height=2.5474130370370385 connect=center]
  Pad9 = Pad [width=1.8822152592592643 height=1.7007567185185211 connect=center]
  Pad10 = Pad [width=1.8822152592592643 height=1.7007567185185211 connect=center]
  Attiny85 = attiny85 [package=dip]
  Pad11 = Pad [width=1.6000000000000001 height=3.2999999999999998 connect=center]
  Pad12 = Pad [width=1.6000000000000001 height=3.2999999999999998 connect=center]
  Pad13 = Pad [width=1.6000000000000001 height=3.2999999999999998 connect=center]
  Pad14 = Pad [width=1.6000000000000001 height=3.2999999999999998 connect=center]
  Pad15 = Pad [width=1.6000000000000001 height=3.2999999999999998 connect=center]
  Pad16 = Pad [width=1.6000000000000001 height=3.2999999999999998 connect=center]
  Pad17 = Pad [width=1.6000000000000001 height=3.2999999999999998 connect=center]
  Pad18 = Pad [width=1.6000000000000001 height=3.2999999999999998 connect=center]
  J13 = Generic female header - 1 pins [form="♀ (female)" package=THT]  # not connected
  J14 = Generic female header - 1 pins [form="♀ (female)" package=THT]  # not connected
  J15 = Generic female header - 1 pins [form="♀ (female)" package=THT]  # not connected
  10uF = Electrolytic Capacitor [capacitance=1µF package="100 mil [THT, electrolytic]"]
  100nF = Ceramic Capacitor [capacitance=100nF package="100 mil [THT, multilayer]"]
  S4 = Toggle Switch [package=THT]
  S5 = Toggle Switch [package=THT]
  7805 = Voltage Regulator - 5V [package="TO220 [THT]"]
  Pad19 = Pad [width=1.6000000000000001 height=3.2999999999999998 connect=center]
  Pad20 = Pad [width=1.6000000000000001 height=3.2999999999999998 connect=center]
  R2 = Rotary Potentiometer (Small) [maximum_resistance=10kΩ package=THT]
  U1 = TOUCH [package=touch2]
  1M = TRIMPOT [package=trim_pot_pth]
  J7 = Generic female header - 1 pins [form="♀ (female)" package=THT]  # not connected
  J4 = Generic female header - 1 pins [form="♀ (female)" package=THT]  # not connected
  J11 = Generic female header - 1 pins [form="♀ (female)" package=THT]  # not connected
  J10 = Generic female header - 1 pins [form="♀ (female)" package=THT]  # not connected
  J8 = Generic female header - 1 pins [form="♀ (female)" package=THT]  # not connected
  J9 = Generic female header - 1 pins [form="♀ (female)" package=THT]  # not connected
  J12 = Generic female header - 1 pins [form="♀ (female)" package=THT]  # not connected
  R1 = Rotary Potentiometer (Small) [maximum_resistance=100kΩ package=THT]

nets:
  GND: OUT.Sleeve, USB-B.GND, USB-B.chassis5, USB-B.chassis6, 3V6.anode, 3V6_2.anode, 7/12V.GND, J1.pin4, BAT2.V+, LED1.cathode, BC548.E, Pad8.pad, Attiny85.Pin_4, Pad15.pad, 10uF.-, 100nF.1, 7805.GND, R2.leg1, U1.T2, R1.leg1
  N1: OUT.Ring, ring.pin1
  N2: OUT.Tip, R2.wiper
  N3: S1.2, S1.5, 1N4007.cathode
  N4: S1.1, S1.4
  N5: S1.3, S1.6, J1.pin9, 10uF.+, 7805.input_voltage
  N6: USB-B.5V, Pad9.pad
  N7: USB-B.d-, 3V6_2.cathode, 1K5Ω_2.Pin_1, 68Ω_2.Pin_1
  N8: USB-B.d+, 3V6.cathode, 68Ω.Pin_1
  N9: 7/12V.VCC, BAT2.V-, 1N4007.anode
  N10: J1.pin1, Attiny85.Pin_5, Pad14.pad, R2.leg2
  N11: J1.pin2, 1K5Ω.Pin_1, 1K5Ω_2.Pin_0, Pad7.pad, Pad10.pad, Attiny85.Pin_8, Pad11.pad, 100nF.0, 7805.output_voltage, 1M.WIPER, R1.leg2
  N12: J1.pin3, 330Ω.Pin_1
  N13: J1.pin5, BC548.C
  N14: J1.pin6, Pad2.pad, Attiny85.Pin_3, Pad16.pad, S5.COM
  N15: J1.pin7, Pad6.pad, Attiny85.Pin_2, Pad17.pad, S4.COM, U1.T1
  N16: J1.pin8, Attiny85.Pin_1, Pad18.pad
  N17: Pad1.pad, 68Ω.Pin_0, S5.L1
  N18: Pad3.pad, S5.L2, R1.wiper
  N19: Pad4.pad, 68Ω_2.Pin_0, S4.L1
  N20: Pad5.pad, S4.L2, Pad20.pad, 1M.CCW
  N21: 1K5Ω.Pin_0, LED1.anode
  N22: 330Ω.Pin_0, Attiny85.Pin_7, Pad12.pad
  N23: BC548.B, 1KΩ.Pin_0
  N24: 1KΩ.Pin_1, Attiny85.Pin_6, Pad13.pad
  N25: Pad19.pad, 1M.CW

notes:
  GAMELIN (USB version), laboratoriodejuguete.com
  github.com/labodejuguete/gamelin
  -
  +
  +•)-

custom parts:
  Generic female header - 1 pins: Generic female header
  Generic female header - 1 pins: Generic female header
  Generic female header - 1 pins: Generic female header
  TOUCH: Electrode for resistive touch detection
  Generic female header - 1 pins: Generic female header
  Generic female header - 1 pins: Generic female header
  Generic female header - 1 pins: Generic female header
  Generic female header - 1 pins: Generic female header
  Generic female header - 1 pins: Generic female header
  Generic female header - 1 pins: Generic female header
  Generic female header - 1 pins: Generic female header
